// Logisim project FinalQ5.circ as structural Verilog: 1 circuit, main circuit main
module main (
  input  RESET,
  output [1:0] C
);

  wire CLK_out, d_ff_1_qn, d_ff_2_qn;

  Clock CLK (.out(CLK_out));
  D_Flip_Flop d_ff_1 (.D(d_ff_1_qn), .clk(CLK_out), .Q(C[0]), .Qn(d_ff_1_qn), .reset(RESET));  // open: preset
  D_Flip_Flop d_ff_2 (.D(d_ff_2_qn), .clk(d_ff_1_qn), .Q(C[1]), .Qn(d_ff_2_qn), .reset(RESET));  // open: preset
endmodule
