// Logisim project HW2.circ as structural Verilog: 5 circuits, main circuit main
module main (
);

  // AND_Gate and_1 is placed but not wired
endmodule

module Problem1 (
  input  A,
  input  B,
  input  C,
  input  A_2,
  input  B_2,
  input  C_2,
  output Y,
  output out_8
);

  wire and_1_out, and_2_out, and_3_out, and_4_out, and_5_out, not_1_out, not_2_out;

  and and_1 (and_1_out, A_2, B_2);
  and and_2 (and_2_out, C_2, B_2, not_1_out);
  not not_1 (not_1_out, A_2);
  nor nor_1 (out_8, and_1_out, and_2_out);
  and and_3 (and_3_out, A, B);
  and and_4 (and_4_out, B, C);
  and and_5 (and_5_out, C, B, not_2_out);
  not not_2 (not_2_out, A);
  nor nor_2 (Y, and_3_out, and_4_out, and_5_out);

  // Notes on the sheet:
  //   Original Circuit
endmodule

module Problem2q2 (
  input  M3,
  input  M2,
  input  M1,
  input  M0,
  output q2
);

  wire and_1_out, and_2_out, not_1_out, not_2_out;

  not not_1 (not_1_out, M2);
  not not_2 (not_2_out, M0);
  and and_1 (and_1_out, not_1_out, not_2_out);
  and and_2 (and_2_out, not_2_out, M1);
  or or_1 (q2, and_1_out, and_2_out);
endmodule

module Problem2 (
  input  M3,
  input  M2,
  input  M1,
  input  M0,
  output q5,
  output q2
);

  wire and_1_out, and_2_out, and_3_out, and_4_out, not_1_out, not_2_out, not_3_out;

  not not_1 (not_1_out, M2);
  not not_2 (not_2_out, M1);
  not not_3 (not_3_out, M0);
  and and_1 (and_1_out, not_2_out, not_3_out);
  and and_2 (and_2_out, M1, M0);
  and and_3 (and_3_out, not_1_out, not_3_out);
  and and_4 (and_4_out, M1, not_3_out);
  or or_1 (q5, not_1_out, and_1_out, and_2_out);
  or or_2 (q2, and_3_out, and_4_out);
endmodule

module Problem3 (
  input  [5:0] in_1,
  output [15:0] out_2,
  output [15:0] out_3,
  output [15:0] out_4,
  output [15:0] out_5
);

  wire decoder_1_out0, decoder_1_out1, decoder_1_out2, decoder_1_out3;

  Decoder #(.select(2)) decoder_1 (
    .out0(decoder_1_out0), .out1(decoder_1_out1), .out2(decoder_1_out2), .out3(decoder_1_out3),
    .sel(in_1[5:4]), .en(1'b1));
  Decoder #(.select(4)) decoder_2 (
    .out0(out_2[0]), .out1(out_2[1]), .out2(out_2[2]), .out3(out_2[3]), .out4(out_2[4]), .out5(out_2[5]),
    .out6(out_2[6]), .out7(out_2[7]), .out8(out_2[8]), .out9(out_2[9]), .out10(out_2[10]), .out11(out_2[11]),
    .out12(out_2[12]), .out13(out_2[13]), .out14(out_2[14]), .out15(out_2[15]), .sel(in_1[3:0]),
    .en(decoder_1_out0));
  Decoder #(.select(4)) decoder_3 (
    .out0(out_3[0]), .out1(out_3[1]), .out2(out_3[2]), .out3(out_3[3]), .out4(out_3[4]), .out5(out_3[5]),
    .out6(out_3[6]), .out7(out_3[7]), .out8(out_3[8]), .out9(out_3[9]), .out10(out_3[10]), .out11(out_3[11]),
    .out12(out_3[12]), .out13(out_3[13]), .out14(out_3[14]), .out15(out_3[15]), .sel(in_1[3:0]),
    .en(decoder_1_out1));
  Decoder #(.select(4)) decoder_4 (
    .out0(out_4[0]), .out1(out_4[1]), .out2(out_4[2]), .out3(out_4[3]), .out4(out_4[4]), .out5(out_4[5]),
    .out6(out_4[6]), .out7(out_4[7]), .out8(out_4[8]), .out9(out_4[9]), .out10(out_4[10]), .out11(out_4[11]),
    .out12(out_4[12]), .out13(out_4[13]), .out14(out_4[14]), .out15(out_4[15]), .sel(in_1[3:0]),
    .en(decoder_1_out2));
  Decoder #(.select(4)) decoder_5 (
    .out0(out_5[0]), .out1(out_5[1]), .out2(out_5[2]), .out3(out_5[3]), .out4(out_5[4]), .out5(out_5[5]),
    .out6(out_5[6]), .out7(out_5[7]), .out8(out_5[8]), .out9(out_5[9]), .out10(out_5[10]), .out11(out_5[11]),
    .out12(out_5[12]), .out13(out_5[13]), .out14(out_5[14]), .out15(out_5[15]), .sel(in_1[3:0]),
    .en(decoder_1_out3));

  // Notes on the sheet:
  //   A[5:0]
  //   X0
  //   X1
  //   X2
  //   X3
endmodule
