// Logisim project HW1Q7.circ as structural Verilog: 1 circuit, main circuit Test
module Test (
  input  [3:0] M,
  output Y
);

  wire nor_1_out, nor_2_out, not_1_out, not_2_out;

  not not_1 (not_1_out, M[3]);
  not not_2 (not_2_out, M[0]);
  nor nor_1 (nor_1_out, not_1_out, not_2_out);
  nor nor_2 (nor_2_out, M[3], M[0]);
  nor nor_3 (Y, nor_1_out, nor_2_out);
endmodule
