// Logisim project HW3Q3.circ as structural Verilog: 2 circuits, main circuit main
module main (
  input  X,
  input  RESET,
  output Y_1,
  output Y_0
);

  wire and_1_out, and_2_out, and_3_out, CLK_out, not_1_out, not_2_out, or_1_out;

  Clock CLK (.out(CLK_out));
  not not_1 (not_1_out, Y_0);
  and and_1 (and_1_out, Y_0, X);
  and and_2 (and_2_out, not_1_out, Y_1);
  not not_2 (not_2_out, Y_1);
  or or_1 (or_1_out, and_1_out, and_2_out);
  and and_3 (and_3_out, not_2_out, X);
  D_Flip_Flop d_ff_1 (.D(or_1_out), .clk(CLK_out), .Q(Y_1), .reset(RESET));  // open: Qn, preset
  D_Flip_Flop d_ff_2 (.D(and_3_out), .clk(CLK_out), .Q(Y_0), .reset(RESET));  // open: Qn, preset
endmodule

module OtherMethdo (
  input  in_1,
  output Y_1,
  output Y_0
);

  wire and_1_out, and_2_out, and_3_out, and_4_out, not_1_out;

  and and_1 (and_1_out, Y_1, Y_0);
  and and_2 (and_2_out, Y_1, in_1);
  and and_3 (and_3_out, in_1, Y_0);
  and and_4 (and_4_out, in_1, not_1_out);
  not not_1 (not_1_out, Y_0);
  or or_1 (Y_1, and_1_out, and_2_out, and_3_out);
  or or_2 (Y_0, and_1_out, and_4_out);
endmodule
